// Logisim project full_project(2).circ as structural Verilog: 12 circuits, main circuit mem
module main (
  output [3:0] icode,
  output [3:0] ifun,
  output [3:0] rA,
  output [3:0] rB,
  output [63:0] valE,
  output [63:0] valC,
  output [11:0] valP,
  output [63:0] valM,
  output [63:0] valA,
  output [11:0] PC,
  output [63:0] valB,
  output [2:0] CC,
  output [7:0] cycle_number
);

  wire and_1_out, and_2_out, and_3_out, and_4_out, and_5_out, clock_1_out, comparator_1_eq, decoder_1_out2,
       decoder_1_out11, decoder_1_out12, decoder_1_out13, decoder_1_out14, decoder_1_out15, decoder_1_out16,
       decoder_1_out17, decoder_1_out18, decoder_1_out19, decoder_1_out20, decoder_1_out21, ex_1_cnd,
       ex_1_setrbtozero, halt_q, or_1_out;
  wire [11:0] pc_update_1_newpc;
  wire [63:0] deco_1_r8, deco_1_r9, deco_1_r10, deco_1_r12, deco_1_r13, deco_1_r14, deco_1_rax, deco_1_rbp,
       deco_1_rcx, deco_1_rdi, deco_1_rdx, deco_1_rsi, deco_1_rsp, r10_q, rbx_p1;

  Clock clock_1 (.out(clock_1_out));
  and and_1 (and_1_out, ~halt_q, clock_1_out);  // AND_Gate
  Register #(.width(64)) rax (.D(deco_1_rax), .en(1'b1), .clk(and_1_out));  // open: Q, clr
  Register #(.width(64)) r8 (.D(deco_1_r8), .en(1'b1), .clk(and_1_out));  // open: Q, clr
  Register #(.width(64)) rcx (.en(1'b1), .clk(and_1_out));  // open: D, Q, clr
  Register #(.width(64)) r9 (.D(deco_1_r9), .en(1'b1), .clk(and_1_out));  // open: Q, clr
  fetch fetch_1 (
    .newPc(pc_update_1_newpc), .clk(and_1_out), .setRbToZero(ex_1_setrbtozero), .PC(PC), .icode(icode),
    .ifun(ifun), .rA(rA), .rB(rB), .valC(valC), .valP(valP), .cycle_number(cycle_number));
  Register #(.width(64)) rdx (.D(deco_1_rdx), .en(1'b1), .clk(and_1_out));  // open: Q, clr
  Register #(.width(64)) r10 (.D(deco_1_r10), .en(1'b1), .clk(and_1_out), .Q(r10_q));  // open: clr
  Decoder #(.enable("false"), .select(5)) decoder_1 (
    .out2(decoder_1_out2), .out11(decoder_1_out11), .out12(decoder_1_out12), .out13(decoder_1_out13),
    .out14(decoder_1_out14), .out15(decoder_1_out15), .out16(decoder_1_out16), .out17(decoder_1_out17),
    .out18(decoder_1_out18), .out19(decoder_1_out19), .out20(decoder_1_out20), .out21(decoder_1_out21),
    .sel(cycle_number[4:0]));  // open: out0, out1, out3, out4, out5, out6, out7, out8, out9, out10, out22, out23, out24, out25, out26, out27, out28, out29, out30, out31
  // Register #(.width(64)) rbx: pin names not known; wires that end beside it: rbx_p1, 1'b1, and_1_out
  Register #(.width(64)) r11 (.D(r10_q), .en(1'b1), .clk(and_1_out));  // open: Q, clr
  Comparator #(.width(4)) comparator_1 (.a(4'b0000), .b(icode), .eq(comparator_1_eq));  // open: gt, lt
  Register #(.width(64)) rsp (.D(deco_1_rsp), .en(1'b1), .clk(and_1_out));  // open: Q, clr
  Register #(.width(64)) r12 (.D(deco_1_r12), .en(1'b1), .clk(and_1_out));  // open: Q, clr
  and and_2 (and_2_out, decoder_1_out2, and_1_out);
  Register #(.width(1)) halt (.D(comparator_1_eq), .en(1'b1), .clk(and_2_out), .Q(halt_q));  // open: clr
  deco deco_1 (
    .rA(rA), .rB(rB), .icode(icode), .CC(CC), .valE(valE), .valM(valM), .clk(and_4_out),
    .cycle(cycle_number), .valB(valB), .r14(deco_1_r14), .r13(deco_1_r13), .valA(valA), .r12(deco_1_r12),
    .r11(r10_q), .r10(deco_1_r10), .r9(deco_1_r9), .r8(deco_1_r8), .rdi(deco_1_rdi), .rsi(deco_1_rsi),
    .rbp(deco_1_rbp), .rsp(deco_1_rsp), .rbx(rbx_p1), .rdx(deco_1_rdx), .rcx(deco_1_rcx), .rax(deco_1_rax));
  and and_3 (and_3_out, and_1_out, decoder_1_out11);
  Register #(.width(64)) rbp (.D(deco_1_rbp), .en(1'b1), .clk(and_1_out));  // open: Q, clr
  Register #(.width(64)) r13 (.D(deco_1_r13), .en(1'b1), .clk(and_1_out));  // open: Q, clr
  or or_1 (or_1_out, decoder_1_out12, decoder_1_out13, decoder_1_out14, decoder_1_out15, decoder_1_out16, decoder_1_out17, decoder_1_out18, decoder_1_out19, decoder_1_out20);
  and and_4 (and_4_out, decoder_1_out21, and_1_out);
  Register #(.width(64)) rsi (.D(deco_1_rsi), .en(1'b1), .clk(and_1_out));  // open: Q, clr
  Register #(.width(64)) r14 (.D(deco_1_r14), .en(1'b1), .clk(and_1_out));  // open: Q, clr
  and and_5 (and_5_out, and_1_out, or_1_out);
  Register #(.width(64)) rdi (.D(deco_1_rdi), .en(1'b1), .clk(and_1_out));  // open: Q, clr
  ex ex_1 (
    .clk(and_3_out), .icode(icode), .valA(valA), .valC(valC), .valB(valB), .ifun(ifun), .CC(CC),
    .cnd(ex_1_cnd), .setRbToZero(ex_1_setrbtozero), .valE(valE));
  mem mem_1 (.clk(and_5_out), .icode(icode), .valE(valE), .valA(valA), .valP(valP), .valM(valM));
  pc_update pc_update_1 (
    .icode(icode), .cnd(ex_1_cnd), .valC(valC), .valP(valP), .valM(valM), .newPC(pc_update_1_newpc));
endmodule

module mem (
  input  clk,
  input  [3:0] icode,
  input  [63:0] valE,
  input  [63:0] valA,
  input  [11:0] valP,
  output [63:0] valM
);

  wire and_1_out, and_2_out, comparator_1_eq, comparator_2_gt, comparator_3_lt, decoder_1_out4,
       decoder_1_out5, decoder_1_out8, decoder_1_out9, decoder_1_out10, decoder_1_out11, decoder_2_out0,
       decoder_2_out1, decoder_2_out2, decoder_2_out3, decoder_2_out4, decoder_2_out5, decoder_2_out6,
       decoder_2_out7, or_1_out, or_2_out, or_3_out, or_4_out, or_5_out;
  wire [2:0] bit_extender_5_out, subtractor_1_out;
  wire [7:0] adder_1_out, demultiplexer_1_out0, demultiplexer_1_out1, demultiplexer_1_out2,
       demultiplexer_1_out3, demultiplexer_1_out4, demultiplexer_1_out5, demultiplexer_1_out6,
       demultiplexer_1_out7, multiplexer_1_out, multiplexer_2_out, multiplexer_3_out, multiplexer_5_out,
       ram_1_dout, register_1_q;
  wire [11:0] adder_2_out, bit_extender_1_out, bit_extender_2_out, bit_extender_4_out, multiplexer_4_out;
  wire [63:0] bit_extender_3_out;

  Bit_Extender #(.in_width(64), .out_width(12), .\type ("zero")) bit_extender_1 (.in(valE), .out(bit_extender_1_out));
  Bit_Extender #(.in_width(64), .out_width(12), .\type ("zero")) bit_extender_2 (.in(valA), .out(bit_extender_2_out));
  assign bit_extender_3_out = {{52{1'b0}}, valP};  // Bit_Extender bit_extender_3
  Decoder #(.select(4)) decoder_1 (
    .out4(decoder_1_out4), .out5(decoder_1_out5), .out8(decoder_1_out8), .out9(decoder_1_out9),
    .out10(decoder_1_out10), .out11(decoder_1_out11), .sel(icode), .en(1'b1));  // open: out0, out1, out2, out3, out6, out7, out12, out13, out14, out15
  Multiplexer #(.select(3), .width(8)) multiplexer_1 (
    .in0(valA[7:0]), .in1(valA[15:8]), .in2(valA[23:16]), .in3(valA[31:24]), .in4(valA[39:32]),
    .in5(valA[47:40]), .in6(valA[55:48]), .in7(valA[63:56]), .out(multiplexer_1_out), .sel(bit_extender_5_out));
  Multiplexer #(.select(3), .width(8)) multiplexer_2 (
    .in0(bit_extender_3_out[7:0]), .in1(bit_extender_3_out[15:8]), .in2(bit_extender_3_out[23:16]),
    .in3(bit_extender_3_out[31:24]), .in4(bit_extender_3_out[39:32]), .in5(bit_extender_3_out[47:40]),
    .in6(bit_extender_3_out[55:48]), .in7(bit_extender_3_out[63:56]), .out(multiplexer_2_out),
    .sel(bit_extender_5_out));
  Multiplexer #(.width(8)) multiplexer_3 (
    .in0(adder_1_out), .in1({8{1'b0}}), .out(multiplexer_3_out), .sel(comparator_1_eq));
  or or_1 (or_1_out, decoder_1_out9, decoder_1_out11);
  or or_2 (or_2_out, decoder_1_out10, decoder_1_out4);
  Register register_1 (.D(multiplexer_3_out), .en(1'b1), .clk(and_1_out), .Q(register_1_q));  // open: clr
  Multiplexer #(.width(12)) multiplexer_4 (
    .in0(bit_extender_1_out), .in1(bit_extender_2_out), .out(multiplexer_4_out), .sel(or_1_out));
  or or_3 (or_3_out, decoder_1_out10, decoder_1_out4, decoder_1_out8);
  or or_4 (or_4_out, decoder_1_out11, decoder_1_out5, decoder_1_out9);
  Multiplexer #(.width(8)) multiplexer_5 (
    .in0(multiplexer_2_out), .in1(multiplexer_1_out), .out(multiplexer_5_out), .sel(or_2_out));
  or or_5 (or_5_out, decoder_1_out4, decoder_1_out5, decoder_1_out8, decoder_1_out9, decoder_1_out10, decoder_1_out11);
  Comparator comparator_1 (.a(register_1_q), .b(8'h19), .eq(comparator_1_eq));  // open: gt, lt
  assign bit_extender_4_out = {{4{1'b0}}, register_1_q};  // Bit_Extender bit_extender_4
  and and_1 (and_1_out, clk, or_5_out);
  Adder adder_1 (.a(register_1_q), .b(8'h1), .out(adder_1_out));  // open: cin, cout
  Adder #(.width(12)) adder_2 (.a(multiplexer_4_out), .b(bit_extender_4_out), .out(adder_2_out));  // open: cin, cout
  Bit_Extender #(.out_width(3), .\type ("zero")) bit_extender_5 (.in(register_1_q), .out(bit_extender_5_out));
  RAM #(.addrWidth(12)) ram_1 (
    .addr(adder_2_out), .we(and_2_out), .oe(or_4_out), .clk(and_1_out), .din(multiplexer_5_out),
    .dout(ram_1_dout));
  and and_2 (and_2_out, or_3_out, comparator_2_gt);
  Comparator comparator_2 (.a(8'h8), .b(register_1_q), .gt(comparator_2_gt));  // open: eq, lt
  Subtractor #(.width(3)) subtractor_1 (.a(bit_extender_5_out), .b(3'b001), .out(subtractor_1_out));  // open: bin, bout
  Comparator comparator_3 (.a(register_1_q), .b(8'h9), .lt(comparator_3_lt));  // open: gt, eq
  Register register_2 (.D(demultiplexer_1_out7), .en(decoder_2_out7), .clk(clk), .Q(valM[63:56]));  // open: clr
  Register register_3 (.D(demultiplexer_1_out6), .en(decoder_2_out6), .clk(clk), .Q(valM[55:48]));  // open: clr
  Register register_4 (.D(demultiplexer_1_out5), .en(decoder_2_out5), .clk(clk), .Q(valM[47:40]));  // open: clr
  Decoder #(.select(3)) decoder_2 (
    .out0(decoder_2_out0), .out1(decoder_2_out1), .out2(decoder_2_out2), .out3(decoder_2_out3),
    .out4(decoder_2_out4), .out5(decoder_2_out5), .out6(decoder_2_out6), .out7(decoder_2_out7),
    .sel(subtractor_1_out), .en(comparator_3_lt));
  Register register_5 (.D(demultiplexer_1_out4), .en(decoder_2_out4), .clk(clk), .Q(valM[39:32]));  // open: clr
  Register register_6 (.D(demultiplexer_1_out3), .en(decoder_2_out3), .clk(clk), .Q(valM[31:24]));  // open: clr
  Demultiplexer #(.select(3), .width(8)) demultiplexer_1 (
    .out0(demultiplexer_1_out0), .out1(demultiplexer_1_out1), .out2(demultiplexer_1_out2),
    .out3(demultiplexer_1_out3), .out4(demultiplexer_1_out4), .out5(demultiplexer_1_out5),
    .out6(demultiplexer_1_out6), .out7(demultiplexer_1_out7), .in(ram_1_dout), .sel(subtractor_1_out));
  Register register_7 (.D(demultiplexer_1_out2), .en(decoder_2_out2), .clk(clk), .Q(valM[23:16]));  // open: clr
  Register register_8 (.D(demultiplexer_1_out1), .en(decoder_2_out1), .clk(clk), .Q(valM[15:8]));  // open: clr
  Register register_9 (.D(demultiplexer_1_out0), .en(decoder_2_out0), .clk(clk), .Q(valM[7:0]));  // open: clr

  // Notes on the sheet:
  //   icode decoded output
  //   last cycle number
  //   mem address in
  //   mem data in
endmodule

module dec (
  input  wb_enable,
  input  write_to_register_enable,
  input  [2:0] srcA_address,
  input  [7:0] srcA_data,
  input  [2:0] srcB_address,
  input  [7:0] srcB_data,
  input  [2:0] destE,
  input  [7:0] valE,
  input  [2:0] destM,
  input  [7:0] valM,
  output [7:0] valA,
  output [7:0] valB
);

  wire clock_1_out, demultiplexer_1_out0, demultiplexer_1_out1, demultiplexer_1_out2, demultiplexer_1_out3,
       demultiplexer_1_out4, demultiplexer_1_out5, demultiplexer_1_out6, demultiplexer_1_out7,
       demultiplexer_2_out0, demultiplexer_2_out1, demultiplexer_2_out2, demultiplexer_2_out3,
       demultiplexer_2_out4, demultiplexer_2_out5, demultiplexer_2_out6, demultiplexer_2_out7, or_1_out,
       or_3_out, or_5_out, or_7_out, or_9_out, or_11_out, or_13_out, or_15_out;
  wire [2:0] multiplexer_2_out, multiplexer_3_out;
  wire [7:0] demultiplexer_3_out0, demultiplexer_3_out1, demultiplexer_3_out2, demultiplexer_3_out3,
       demultiplexer_3_out4, demultiplexer_3_out5, demultiplexer_3_out6, demultiplexer_3_out7,
       demultiplexer_4_out0, demultiplexer_4_out1, demultiplexer_4_out2, demultiplexer_4_out3,
       demultiplexer_4_out4, demultiplexer_4_out5, demultiplexer_4_out6, demultiplexer_4_out7,
       multiplexer_1_out, multiplexer_4_out, or_2_out, or_4_out, or_6_out, or_8_out, or_10_out, or_12_out,
       or_14_out, or_16_out, register_1_q, register_2_q, register_3_q, register_4_q, register_5_q,
       register_6_q, register_7_q, register_8_q;

  Multiplexer #(.width(8)) multiplexer_1 (.in0(srcA_data), .in1(valE), .out(multiplexer_1_out), .sel(wb_enable));
  Demultiplexer #(.select(3)) demultiplexer_1 (
    .out0(demultiplexer_1_out0), .out1(demultiplexer_1_out1), .out2(demultiplexer_1_out2),
    .out3(demultiplexer_1_out3), .out4(demultiplexer_1_out4), .out5(demultiplexer_1_out5),
    .out6(demultiplexer_1_out6), .out7(demultiplexer_1_out7), .in(write_to_register_enable),
    .sel(multiplexer_2_out));
  Multiplexer #(.width(3)) multiplexer_2 (.in0(srcA_address), .in1(destE), .out(multiplexer_2_out), .sel(wb_enable));
  Demultiplexer #(.select(3)) demultiplexer_2 (
    .out0(demultiplexer_2_out0), .out1(demultiplexer_2_out1), .out2(demultiplexer_2_out2),
    .out3(demultiplexer_2_out3), .out4(demultiplexer_2_out4), .out5(demultiplexer_2_out5),
    .out6(demultiplexer_2_out6), .out7(demultiplexer_2_out7), .in(write_to_register_enable),
    .sel(multiplexer_3_out));
  Multiplexer #(.width(3)) multiplexer_3 (.in0(srcB_address), .in1(destM), .out(multiplexer_3_out), .sel(wb_enable));
  Multiplexer #(.width(8)) multiplexer_4 (.in0(srcB_data), .in1(valM), .out(multiplexer_4_out), .sel(wb_enable));
  or or_1 (or_1_out, demultiplexer_1_out0, demultiplexer_2_out0);
  Demultiplexer #(.select(3), .width(8)) demultiplexer_3 (
    .out0(demultiplexer_3_out0), .out1(demultiplexer_3_out1), .out2(demultiplexer_3_out2),
    .out3(demultiplexer_3_out3), .out4(demultiplexer_3_out4), .out5(demultiplexer_3_out5),
    .out6(demultiplexer_3_out6), .out7(demultiplexer_3_out7), .in(multiplexer_1_out), .sel(multiplexer_2_out));
  Demultiplexer #(.select(3), .width(8)) demultiplexer_4 (
    .out0(demultiplexer_4_out0), .out1(demultiplexer_4_out1), .out2(demultiplexer_4_out2),
    .out3(demultiplexer_4_out3), .out4(demultiplexer_4_out4), .out5(demultiplexer_4_out5),
    .out6(demultiplexer_4_out6), .out7(demultiplexer_4_out7), .in(multiplexer_4_out), .sel(multiplexer_3_out));
  Register register_1 (.D(or_2_out), .en(or_1_out), .clk(clock_1_out), .Q(register_1_q));  // open: clr
  Clock clock_1 (.out(clock_1_out));
  assign or_2_out = demultiplexer_3_out0 | demultiplexer_4_out0;  // OR_Gate or_2, 8 bits wide
  or or_3 (or_3_out, demultiplexer_1_out1, demultiplexer_2_out1);
  Multiplexer #(.select(3), .width(8)) multiplexer_5 (
    .in0(register_1_q), .in1(register_2_q), .in2(register_3_q), .in3(register_4_q), .in4(register_5_q),
    .in5(register_6_q), .in6(register_7_q), .in7(register_8_q), .out(valA), .sel(srcA_address));
  Register register_2 (.D(or_4_out), .en(or_3_out), .clk(clock_1_out), .Q(register_2_q));  // open: clr
  assign or_4_out = demultiplexer_3_out1 | demultiplexer_4_out1;  // OR_Gate or_4, 8 bits wide
  Register register_3 (.D(or_6_out), .en(or_5_out), .clk(clock_1_out), .Q(register_3_q));  // open: clr
  or or_5 (or_5_out, demultiplexer_1_out2, demultiplexer_2_out2);
  assign or_6_out = demultiplexer_3_out2 | demultiplexer_4_out2;  // OR_Gate or_6, 8 bits wide
  or or_7 (or_7_out, demultiplexer_1_out3, demultiplexer_2_out3);
  assign or_8_out = demultiplexer_3_out3 | demultiplexer_4_out3;  // OR_Gate or_8, 8 bits wide
  Register register_4 (.D(or_8_out), .en(or_7_out), .clk(clock_1_out), .Q(register_4_q));  // open: clr
  Register register_5 (.D(or_10_out), .en(or_9_out), .clk(clock_1_out), .Q(register_5_q));  // open: clr
  or or_9 (or_9_out, demultiplexer_1_out4, demultiplexer_2_out4);
  assign or_10_out = demultiplexer_3_out4 | demultiplexer_4_out4;  // OR_Gate or_10, 8 bits wide
  or or_11 (or_11_out, demultiplexer_1_out5, demultiplexer_2_out5);
  Register register_6 (.D(or_12_out), .en(or_11_out), .clk(clock_1_out), .Q(register_6_q));  // open: clr
  assign or_12_out = demultiplexer_3_out5 | demultiplexer_4_out5;  // OR_Gate or_12, 8 bits wide
  Multiplexer #(.select(3), .width(8)) multiplexer_6 (
    .in0(register_1_q), .in1(register_2_q), .in2(register_3_q), .in3(register_4_q), .in4(register_5_q),
    .in5(register_6_q), .in6(register_7_q), .in7(register_8_q), .out(valB), .sel(srcB_address));
  Register register_7 (.D(or_14_out), .en(or_13_out), .clk(clock_1_out), .Q(register_7_q));  // open: clr
  or or_13 (or_13_out, demultiplexer_1_out6, demultiplexer_2_out6);
  assign or_14_out = demultiplexer_3_out6 | demultiplexer_4_out6;  // OR_Gate or_14, 8 bits wide
  or or_15 (or_15_out, demultiplexer_1_out7, demultiplexer_2_out7);
  Register register_8 (.D(or_16_out), .en(or_15_out), .clk(clock_1_out), .Q(register_8_q));  // open: clr
  assign or_16_out = demultiplexer_3_out7 | demultiplexer_4_out7;  // OR_Gate or_16, 8 bits wide

  // Notes on the sheet:
  //   valA
  //   valB
endmodule

module pc_update (
  input  [3:0] icode,
  input  cnd,
  input  [63:0] valC,
  input  [11:0] valP,
  input  [63:0] valM,
  output [11:0] newPC
);

  wire [11:0] bit_extender_1_out, bit_extender_2_out, multiplexer_1_out;

  Bit_Extender #(.in_width(64), .out_width(12)) bit_extender_1 (.in(valM), .out(bit_extender_1_out));
  Bit_Extender #(.in_width(64), .out_width(12)) bit_extender_2 (.in(valC), .out(bit_extender_2_out));
  Multiplexer #(.width(12)) multiplexer_1 (.in0(valP), .in1(bit_extender_2_out), .out(multiplexer_1_out), .sel(cnd));
  Multiplexer #(.select(4), .width(12)) multiplexer_2 (
    .in0({12{1'b0}}), .in1(valP), .in2(valP), .in3(valP), .in4(valP), .in5(valP), .in6(valP),
    .in7(multiplexer_1_out), .in8(bit_extender_2_out), .in9(bit_extender_1_out), .in10(valP), .in11(valP),
    .out(newPC), .sel(icode));  // open: in12, in13, in14, in15
endmodule

module align (
  input  [7:0] byte0,
  input  [7:0] byte1,
  input  [7:0] byte2,
  input  [7:0] byte3,
  input  [7:0] byte4,
  input  [7:0] byte5,
  input  [7:0] byte6,
  input  [7:0] byte7,
  input  [7:0] byte8,
  input  [7:0] byte9,
  output [3:0] icode,
  output [3:0] ifun,
  output [3:0] rA,
  output [3:0] rB,
  output [63:0] valC,
  output regid,
  output inputvalC
);

  wire demultiplexer_1_out2, demultiplexer_1_out3, demultiplexer_1_out4, demultiplexer_1_out5,
       demultiplexer_1_out6, demultiplexer_1_out7, demultiplexer_1_out8, demultiplexer_1_out10,
       demultiplexer_1_out11, or_1_out, or_4_out;

  Demultiplexer #(.select(4)) demultiplexer_1 (
    .out2(demultiplexer_1_out2), .out3(demultiplexer_1_out3), .out4(demultiplexer_1_out4),
    .out5(demultiplexer_1_out5), .out6(demultiplexer_1_out6), .out7(demultiplexer_1_out7),
    .out8(demultiplexer_1_out8), .out10(demultiplexer_1_out10), .out11(demultiplexer_1_out11), .in(1'b1),
    .sel(byte0[7:4]));  // open: out0, out1, out9, out12, out13, out14, out15
  or or_1 (or_1_out, demultiplexer_1_out2, demultiplexer_1_out3, demultiplexer_1_out4, demultiplexer_1_out5, demultiplexer_1_out6);
  or or_2 (regid, demultiplexer_1_out2, demultiplexer_1_out3, demultiplexer_1_out4, demultiplexer_1_out5, demultiplexer_1_out6, demultiplexer_1_out10, demultiplexer_1_out11);
  or or_3 (inputvalC, demultiplexer_1_out3, demultiplexer_1_out4, demultiplexer_1_out5, demultiplexer_1_out7, demultiplexer_1_out8);
  Multiplexer #(.width(4)) multiplexer_1 (.in0(4'b1111), .in1(byte1[7:4]), .out(rA), .sel(or_4_out));
  or or_4 (or_4_out, demultiplexer_1_out2, demultiplexer_1_out4, demultiplexer_1_out5, demultiplexer_1_out6, demultiplexer_1_out10, demultiplexer_1_out11);
  Multiplexer #(.width(4)) multiplexer_2 (.in0(4'b1111), .in1(byte1[3:0]), .out(rB), .sel(or_1_out));
  Multiplexer #(.width(64)) multiplexer_3 (
    .in0({byte8, byte7, byte6, byte5, byte4, byte3, byte2, byte1}),
    .in1({byte9, byte8, byte7, byte6, byte5, byte4, byte3, byte2}), .out(valC), .sel(regid));

  assign icode = byte0[7:4];
  assign ifun = byte0[3:0];
endmodule

module fetch (
  input  [11:0] newPc,
  input  clk,
  input  setRbToZero,
  output [11:0] PC,
  output [3:0] icode,
  output [3:0] ifun,
  output [3:0] rA,
  output [3:0] rB,
  output [63:0] valC,
  output [11:0] valP,
  output [7:0] cycle_number
);

  wire align_1_inputvalc, align_1_regid, comparator_1_eq, comparator_2_lt, demultiplexer_1_out0,
       demultiplexer_1_out1, demultiplexer_1_out2, demultiplexer_1_out3, demultiplexer_1_out4,
       demultiplexer_1_out5, demultiplexer_1_out6, demultiplexer_1_out7, demultiplexer_1_out8,
       demultiplexer_1_out9, or_1_out, or_2_out;
  wire [3:0] register_4_q_2;
  wire [7:0] adder_1_out, memory_data, multiplexer_1_out, multiplexer_2_out, register_3_q, register_5_q,
       register_6_q, register_7_q, register_8_q, register_9_q, register_10_q, register_11_q, register_12_q;
  wire [7:4] register_4_q;
  wire [11:0] adder_2_out, register_13_q;

  Multiplexer #(.width(8)) multiplexer_1 (
    .in0(adder_1_out), .in1({8{1'b0}}), .out(multiplexer_1_out), .sel(comparator_1_eq));
  Register register_1 (.D(multiplexer_1_out), .en(1'b1), .clk(clk), .Q(cycle_number));  // open: clr
  Comparator comparator_1 (.a(cycle_number), .b(8'h19), .eq(comparator_1_eq));  // open: gt, lt
  Register #(.width(12)) register_2 (.D(newPc), .en(comparator_1_eq), .clk(clk), .Q(PC));  // open: clr
  Adder adder_1 (.a(cycle_number), .b(8'h1), .out(adder_1_out));  // open: cin, cout
  Demultiplexer #(.select(5)) demultiplexer_1 (
    .out0(demultiplexer_1_out0), .out1(demultiplexer_1_out1), .out2(demultiplexer_1_out2),
    .out3(demultiplexer_1_out3), .out4(demultiplexer_1_out4), .out5(demultiplexer_1_out5),
    .out6(demultiplexer_1_out6), .out7(demultiplexer_1_out7), .out8(demultiplexer_1_out8),
    .out9(demultiplexer_1_out9), .in(1'b1), .sel(cycle_number[4:0]));  // open: out10, out11, out12, out13, out14, out15, out16, out17, out18, out19, out20, out21, out22, out23, out24, out25, out26, out27, out28, out29, out30, out31
  Comparator comparator_2 (.a(8'h2), .b(cycle_number), .lt(comparator_2_lt));  // open: gt, eq
  Register register_3 (.D(memory_data), .en(demultiplexer_1_out0), .clk(clk), .Q(register_3_q));  // open: clr
  or or_1 (or_1_out, demultiplexer_1_out1, setRbToZero);
  Multiplexer #(.width(8)) multiplexer_2 (
    .in0(memory_data), .in1({register_4_q, 4'b1111}), .out(multiplexer_2_out), .sel(comparator_2_lt));
  Register register_4 (
    .D(multiplexer_2_out), .en(or_1_out), .clk(or_2_out), .Q({register_4_q, register_4_q_2}));  // open: clr
  or or_2 (or_2_out, clk, setRbToZero);
  Register register_5 (.D(memory_data), .en(demultiplexer_1_out2), .clk(clk), .Q(register_5_q));  // open: clr
  Register register_6 (.D(memory_data), .en(demultiplexer_1_out3), .clk(clk), .Q(register_6_q));  // open: clr
  Adder #(.width(12)) adder_2 (.a(PC), .b({4'b0000, cycle_number}), .out(adder_2_out));  // open: cin, cout
  Register register_7 (.D(memory_data), .en(demultiplexer_1_out4), .clk(clk), .Q(register_7_q));  // open: clr
  Register register_8 (.D(memory_data), .en(demultiplexer_1_out5), .clk(clk), .Q(register_8_q));  // open: clr
  Register register_9 (.D(memory_data), .en(demultiplexer_1_out6), .clk(clk), .Q(register_9_q));  // open: clr
  ROM #(.addrWidth(12)) memory (.addr(adder_2_out), .data(memory_data));
  Register register_10 (.D(memory_data), .en(demultiplexer_1_out7), .clk(clk), .Q(register_10_q));  // open: clr
  Register register_11 (.D(memory_data), .en(demultiplexer_1_out8), .clk(clk), .Q(register_11_q));  // open: clr
  Register register_12 (.D(memory_data), .en(demultiplexer_1_out9), .clk(clk), .Q(register_12_q));  // open: clr
  align align_1 (
    .byte0(register_3_q), .byte1({register_4_q, register_4_q_2}), .byte2(register_5_q), .byte3(register_6_q),
    .byte4(register_7_q), .byte5(register_8_q), .byte6(register_9_q), .byte7(register_10_q),
    .byte8(register_11_q), .byte9(register_12_q), .icode(icode), .ifun(ifun), .rA(rA), .rB(rB), .valC(valC),
    .regid(align_1_regid), .inputvalC(align_1_inputvalc));
  Register #(.width(12)) register_13 (.D(PC), .en(demultiplexer_1_out0), .clk(clk), .Q(register_13_q));  // open: clr
  PC_incr pc_incr_1 (.PC(register_13_q), .regid(align_1_regid), .valC(align_1_inputvalc), .valP(valP));

  // Notes on the sheet:
  //   last cycle number
  //   contents of memory (hex, n*v repeats v):
  //   30 f4 30 7*0 80 20 7*0 30 f2 a 10*0 90 20 23
  //   memory
endmodule

module PC_incr (
  input  [11:0] PC,
  input  regid,
  input  valC,
  output [11:0] valP
);

  wire [11:0] adder_1_out;

  Adder #(.width(12)) adder_1 (.a(PC), .b({{8{1'b0}}, valC, 2'b00, regid}), .out(adder_1_out));  // open: cin, cout
  Adder #(.width(12)) adder_2 (.a(adder_1_out), .b(12'h1), .out(valP));  // open: cin, cout
endmodule

module ALUA (
  input  [3:0] icode,
  input  [63:0] valA,
  input  [63:0] valC,
  output [63:0] alua_output
);

  Multiplexer #(.select(4), .width(64)) multiplexer_1 (
    .in2(valA), .in3(valC), .in4(valC), .in5(valC), .in6(valA), .in8(64'h8), .in9(64'h8), .in10(64'h8),
    .in11(64'h8), .out(alua_output), .sel(icode));  // open: in0, in1, in7, in12, in13, in14, in15
endmodule

module Alub (
  input  [3:0] icode,
  input  [63:0] valB,
  output [63:0] alub_output
);

  Multiplexer #(.select(4), .width(64)) multiplexer_1 (
    .in2(valB), .in3({64{1'b0}}), .in4(valB), .in5(valB), .in6(valB), .in8(valB), .in9(valB), .in10(valB),
    .in11(valB), .out(alub_output), .sel(icode));  // open: in0, in1, in7, in12, in13, in14, in15
endmodule

module ex (
  input  clk,
  input  [3:0] icode,
  input  [63:0] valA,
  input  [63:0] valC,
  input  [63:0] valB,
  input  [3:0] ifun,
  output [2:0] CC,
  output cnd,
  output setRbToZero,
  output [63:0] valE
);

  wire adder_1_cout, and_2_out, and_3_out, and_6_out, and_7_out, and_8_out, comparator_1_eq, comparator_2_eq,
       comparator_3_eq, decoder_1_out0, decoder_1_out1, decoder_1_out2, decoder_1_out3, decoder_2_out6,
       not_1_out, not_2_out, not_3_out, or_1_out, subtractor_1_bout;
  wire [2:0] or_2_out;
  wire [63:0] adder_1_out, adder_2_out, alua_1_alua_output, alub_1_alub_output, and_1_out, multiplexer_1_out,
       subtractor_1_out, subtractor_2_out, xor_1_out;

  ALUA alua_1 (.icode(icode), .valA(valA), .valC(valC), .alua_output(alua_1_alua_output));
  Alub alub_1 (.icode(icode), .valB(valB), .alub_output(alub_1_alub_output));
  Adder #(.width(64)) adder_1 (
    .a(alua_1_alua_output), .b(alub_1_alub_output), .out(adder_1_out), .cout(adder_1_cout));  // open: cin
  Subtractor #(.width(64)) subtractor_1 (
    .a(alub_1_alub_output), .b(alua_1_alua_output), .out(subtractor_1_out), .bout(subtractor_1_bout));  // open: bin
  Adder #(.width(64)) adder_2 (.a(alua_1_alua_output), .b(alub_1_alub_output), .out(adder_2_out));  // open: cin, cout
  Subtractor #(.width(64)) subtractor_2 (
    .a(alua_1_alua_output), .b(alub_1_alub_output), .out(subtractor_2_out));  // open: bin, bout
  assign and_1_out = alua_1_alua_output & alub_1_alub_output;  // AND_Gate and_1, 64 bits wide
  assign xor_1_out = alua_1_alua_output ^ alub_1_alub_output;  // XOR_Gate xor_1, 64 bits wide
  Multiplexer #(.select(4), .width(64)) multiplexer_1 (
    .in0(adder_1_out), .in1(subtractor_1_out), .in2(and_1_out), .in3(xor_1_out), .out(multiplexer_1_out),
    .sel(ifun));  // open: in4, in5, in6, in7, in8, in9, in10, in11, in12, in13, in14, in15
  Comparator #(.width(64)) comparator_1 (.a({64{1'b0}}), .b(xor_1_out), .eq(comparator_1_eq));  // open: gt, lt
  Register #(.width(3)) register_1 (.D(or_2_out), .en(1'b1), .clk(and_2_out), .Q(CC));  // open: clr
  and and_2 (and_2_out, clk, decoder_2_out6);
  Comparator #(.width(64)) comparator_2 (.a({64{1'b0}}), .b(and_1_out), .eq(comparator_2_eq));  // open: gt, lt
  or or_1 (or_1_out, or_2_out[0], or_2_out[1]);
  not not_1 (not_1_out, or_2_out[1]);
  Multiplexer #(.select(4), .width(64)) multiplexer_2 (
    .in2(adder_2_out), .in3(adder_2_out), .in4(adder_2_out), .in5(adder_2_out), .in6(multiplexer_1_out),
    .in8(subtractor_2_out), .in9(adder_2_out), .in10(subtractor_2_out), .in11(adder_2_out), .out(valE),
    .sel(icode));  // open: in0, in1, in7, in12, in13, in14, in15
  Decoder #(.enable("false"), .select(4)) decoder_1 (
    .out0(decoder_1_out0), .out1(decoder_1_out1), .out2(decoder_1_out2), .out3(decoder_1_out3), .sel(ifun));  // open: out4, out5, out6, out7, out8, out9, out10, out11, out12, out13, out14, out15
  not not_2 (not_2_out, or_2_out[0]);
  and and_3 (and_3_out, not_1_out, or_2_out[0]);
  and and_4 (or_2_out[2], decoder_1_out0, decoder_2_out6, adder_1_cout);
  and and_5 (or_2_out[1], subtractor_1_bout, decoder_2_out6, decoder_1_out1);
  and and_6 (and_6_out, decoder_1_out2, decoder_2_out6, comparator_2_eq);
  Decoder #(.enable("false"), .select(4)) decoder_2 (
    .out6(decoder_2_out6), .sel(icode));  // open: out0, out1, out2, out3, out4, out5, out7, out8, out9, out10, out11, out12, out13, out14, out15
  and and_7 (and_7_out, decoder_1_out3, decoder_2_out6, comparator_1_eq);
  or or_2 (or_2_out[0], and_6_out, and_7_out);
  Multiplexer #(.select(4)) multiplexer_3 (
    .in0(1'b1), .in1(or_1_out), .in2(or_2_out[1]), .in3(or_2_out[0]), .in4(not_2_out), .in5(not_1_out),
    .in6(and_3_out), .out(cnd), .sel(ifun));  // open: in7, in8, in9, in10, in11, in12, in13, in14, in15
  not not_3 (not_3_out, cnd);
  and and_8 (and_8_out, not_3_out, clk);
  Comparator #(.width(4)) comparator_3 (.a(4'b0010), .b(icode), .eq(comparator_3_eq));  // open: gt, lt
  Multiplexer multiplexer_4 (.in0(1'b0), .in1(and_8_out), .out(setRbToZero), .sel(comparator_3_eq));

  // Notes on the sheet:
  //   1: SF
  //   2: OF
  //   0: ZF
endmodule

module alu_fun (
  input  [3:0] icode,
  input  [3:0] ifun
);

  Demultiplexer #(.select(4), .width(4)) demultiplexer_1 (
    .in(ifun), .sel(icode));  // open: out0, out1, out2, out3, out4, out5, out6, out7, out8, out9, out10, out11, out12, out13, out14, out15
endmodule

module deco (
  input  [3:0] rA,
  input  [3:0] rB,
  input  [3:0] icode,
  input  [2:0] CC,
  input  [63:0] valE,
  input  [63:0] valM,
  input  clk,
  input  [7:0] cycle,
  output [63:0] valB,
  output [63:0] r14,
  output [63:0] r13,
  output [63:0] valA,
  output [63:0] r12,
  output [63:0] r11,
  output [63:0] r10,
  output [63:0] r9,
  output [63:0] r8,
  output [63:0] rdi,
  output [63:0] rsi,
  output [63:0] rbp,
  output [63:0] rsp,
  output [63:0] rbx,
  output [63:0] rdx,
  output [63:0] rcx,
  output [63:0] rax
);

  wire comparator_1_lt, decoder_1_out0, decoder_1_out1, decoder_1_out2, decoder_1_out3, decoder_1_out4,
       decoder_1_out5, decoder_1_out6, decoder_1_out7, decoder_1_out8, decoder_1_out9, decoder_1_out10,
       decoder_1_out11, decoder_1_out12, decoder_1_out13, decoder_1_out14, decoder_2_out0, decoder_2_out1,
       decoder_2_out2, decoder_2_out3, decoder_2_out4, decoder_2_out5, decoder_2_out6, decoder_2_out7,
       decoder_2_out8, decoder_2_out9, decoder_2_out10, decoder_2_out11, decoder_2_out12, decoder_2_out13,
       decoder_2_out14, or_1_out, or_2_out, or_3_out, or_4_out, or_5_out, or_6_out, or_7_out, or_8_out,
       or_9_out, or_10_out, or_11_out, or_12_out, or_13_out, or_14_out, or_15_out;
  wire [3:0] multiplexer_1_out, multiplexer_2_out, multiplexer_3_out, multiplexer_4_out;
  wire [63:0] demultiplexer_1_out0, demultiplexer_1_out1, demultiplexer_1_out2, demultiplexer_1_out3,
       demultiplexer_1_out4, demultiplexer_1_out5, demultiplexer_1_out6, demultiplexer_1_out7,
       demultiplexer_1_out8, demultiplexer_1_out9, demultiplexer_1_out10, demultiplexer_1_out11,
       demultiplexer_1_out12, demultiplexer_1_out13, demultiplexer_1_out14, demultiplexer_2_out0,
       demultiplexer_2_out1, demultiplexer_2_out2, demultiplexer_2_out3, demultiplexer_2_out4,
       demultiplexer_2_out5, demultiplexer_2_out6, demultiplexer_2_out7, demultiplexer_2_out8,
       demultiplexer_2_out9, demultiplexer_2_out10, demultiplexer_2_out11, demultiplexer_2_out12,
       demultiplexer_2_out13, demultiplexer_2_out14, multiplexer_5_p2, multiplexer_6_out, multiplexer_8_out,
       multiplexer_9_out, multiplexer_10_out, multiplexer_11_out, multiplexer_12_p2, multiplexer_13_out,
       multiplexer_14_p2, multiplexer_15_out, multiplexer_17_p2, multiplexer_18_out, multiplexer_19_out,
       multiplexer_20_out, multiplexer_21_out;

  Multiplexer #(.select(4), .width(4)) multiplexer_1 (
    .in0(4'b1111), .in1(4'b1111), .in2(rB), .in3(rB), .in4(4'b1111), .in5(4'b1111), .in6(rB), .in7(4'b1111),
    .in8(4'b0100), .in9(4'b0100), .in10(4'b0100), .in11(4'b0100), .in12(4'b1111), .in13(4'b1111),
    .in14(4'b1111), .in15(4'b1111), .out(multiplexer_1_out), .sel(icode));
  Multiplexer #(.select(4), .width(4)) multiplexer_2 (
    .in0(4'b1111), .in1(4'b1111), .in2(4'b1111), .in3(4'b1111), .in4(4'b1111), .in5(rA), .in6(4'b1111),
    .in7(4'b1111), .in8(4'b1111), .in9(4'b1111), .in10(4'b1111), .in11(rA), .in12(4'b1111), .in13(4'b1111),
    .in14(4'b1111), .in15(4'b1111), .out(multiplexer_2_out), .sel(icode));
  Multiplexer #(.select(4), .width(4)) multiplexer_3 (
    .in2(rB), .in3(rB), .in4(rB), .in5(rB), .in6(rB), .in7(rB), .in8(4'b0100), .in9(4'b0100), .in10(4'b0100),
    .in11(4'b0100), .out(multiplexer_3_out), .sel(icode));  // open: in0, in1, in12, in13, in14, in15
  Demultiplexer #(.select(4), .width(64)) demultiplexer_1 (
    .out0(demultiplexer_1_out0), .out1(demultiplexer_1_out1), .out2(demultiplexer_1_out2),
    .out3(demultiplexer_1_out3), .out4(demultiplexer_1_out4), .out5(demultiplexer_1_out5),
    .out6(demultiplexer_1_out6), .out7(demultiplexer_1_out7), .out8(demultiplexer_1_out8),
    .out9(demultiplexer_1_out9), .out10(demultiplexer_1_out10), .out11(demultiplexer_1_out11),
    .out12(demultiplexer_1_out12), .out13(demultiplexer_1_out13), .out14(demultiplexer_1_out14), .in(valE),
    .sel(multiplexer_1_out));  // open: out15
  Demultiplexer #(.select(4), .width(64)) demultiplexer_2 (
    .out0(demultiplexer_2_out0), .out1(demultiplexer_2_out1), .out2(demultiplexer_2_out2),
    .out3(demultiplexer_2_out3), .out4(demultiplexer_2_out4), .out5(demultiplexer_2_out5),
    .out6(demultiplexer_2_out6), .out7(demultiplexer_2_out7), .out8(demultiplexer_2_out8),
    .out9(demultiplexer_2_out9), .out10(demultiplexer_2_out10), .out11(demultiplexer_2_out11),
    .out12(demultiplexer_2_out12), .out13(demultiplexer_2_out13), .out14(demultiplexer_2_out14), .in(valM),
    .sel(multiplexer_2_out));  // open: out15
  Decoder #(.select(4)) decoder_1 (
    .out0(decoder_1_out0), .out1(decoder_1_out1), .out2(decoder_1_out2), .out3(decoder_1_out3),
    .out4(decoder_1_out4), .out5(decoder_1_out5), .out6(decoder_1_out6), .out7(decoder_1_out7),
    .out8(decoder_1_out8), .out9(decoder_1_out9), .out10(decoder_1_out10), .out11(decoder_1_out11),
    .out12(decoder_1_out12), .out13(decoder_1_out13), .out14(decoder_1_out14), .sel(multiplexer_1_out),
    .en(comparator_1_lt));  // open: out15
  Decoder #(.select(4)) decoder_2 (
    .out0(decoder_2_out0), .out1(decoder_2_out1), .out2(decoder_2_out2), .out3(decoder_2_out3),
    .out4(decoder_2_out4), .out5(decoder_2_out5), .out6(decoder_2_out6), .out7(decoder_2_out7),
    .out8(decoder_2_out8), .out9(decoder_2_out9), .out10(decoder_2_out10), .out11(decoder_2_out11),
    .out12(decoder_2_out12), .out13(decoder_2_out13), .out14(decoder_2_out14), .sel(multiplexer_2_out),
    .en(comparator_1_lt));  // open: out15
  Comparator comparator_1 (.a(cycle), .b(8'h15), .lt(comparator_1_lt));  // open: gt, eq
  Multiplexer #(.select(4), .width(4)) multiplexer_4 (
    .in2(rA), .in3(rA), .in4(rA), .in5(rA), .in6(rA), .in7(rA), .in8(rA), .in9(4'b0100), .in10(rA),
    .in11(4'b0100), .out(multiplexer_4_out), .sel(icode));  // open: in0, in1, in12, in13, in14, in15
  Register #(.width(64)) register_1 (.D(multiplexer_5_p2), .en(or_1_out), .clk(clk), .Q(rax));  // open: clr
  or or_1 (or_1_out, decoder_1_out0, decoder_2_out0);
  // Multiplexer #(.width(64)) multiplexer_5: pin names not known; wires that end beside it: demultiplexer_1_out0, multiplexer_5_p2, demultiplexer_2_out0
  Register #(.width(64)) register_2 (.D(multiplexer_6_out), .en(or_2_out), .clk(clk), .Q(rcx));  // open: clr
  or or_2 (or_2_out, decoder_1_out1, decoder_2_out1);
  Multiplexer #(.width(64)) multiplexer_6 (
    .in0(demultiplexer_1_out1), .in1(demultiplexer_2_out1), .out(multiplexer_6_out));  // open: sel
  Multiplexer #(.select(4), .width(64)) multiplexer_7 (
    .in0(rax), .in1(rcx), .in2(rdx), .in3(rbx), .in4(rsp), .in5(rbp), .in6(rsi), .in7(rdi), .in8(r8),
    .in9(r9), .in10(r10), .in11(r11), .in12(r12), .in13(r13), .in14(r14), .in15({64{1'b0}}), .out(valA),
    .sel(multiplexer_4_out));
  Register #(.width(64)) register_3 (.D(multiplexer_8_out), .en(or_3_out), .clk(clk), .Q(rdx));  // open: clr
  or or_3 (or_3_out, decoder_1_out2, decoder_2_out2);
  Multiplexer #(.width(64)) multiplexer_8 (
    .in0(demultiplexer_1_out2), .in1(demultiplexer_2_out2), .out(multiplexer_8_out));  // open: sel
  Register #(.width(64)) register_4 (.D(multiplexer_9_out), .en(or_4_out), .clk(clk), .Q(rbx));  // open: clr
  or or_4 (or_4_out, decoder_1_out3, decoder_2_out3);
  Multiplexer #(.width(64)) multiplexer_9 (
    .in0(demultiplexer_1_out3), .in1(demultiplexer_2_out3), .out(multiplexer_9_out));  // open: sel
  Register #(.width(64)) register_5 (.D(multiplexer_10_out), .en(or_5_out), .clk(clk), .Q(rsp));  // open: clr
  or or_5 (or_5_out, decoder_1_out4, decoder_2_out4);
  Multiplexer #(.width(64)) multiplexer_10 (
    .in0(demultiplexer_1_out4), .in1(demultiplexer_2_out4), .out(multiplexer_10_out));  // open: sel
  Register #(.width(64)) register_6 (.D(multiplexer_11_out), .en(or_6_out), .clk(clk), .Q(rbp));  // open: clr
  or or_6 (or_6_out, decoder_1_out5, decoder_2_out5);
  Multiplexer #(.width(64)) multiplexer_11 (
    .in0(demultiplexer_1_out5), .in1(demultiplexer_2_out5), .out(multiplexer_11_out));  // open: sel
  Register #(.width(64)) register_7 (.D(multiplexer_12_p2), .en(or_7_out), .clk(clk), .Q(rsi));  // open: clr
  or or_7 (or_7_out, decoder_1_out6, decoder_2_out6);
  // Multiplexer #(.width(64)) multiplexer_12: pin names not known; wires that end beside it: demultiplexer_1_out6, multiplexer_12_p2, demultiplexer_2_out6
  Multiplexer #(.width(64)) multiplexer_13 (
    .in0(demultiplexer_1_out7), .in1(demultiplexer_2_out7), .out(multiplexer_13_out));  // open: sel
  Register #(.width(64)) register_8 (.D(multiplexer_13_out), .en(or_8_out), .clk(clk), .Q(rdi));  // open: clr
  or or_8 (or_8_out, decoder_1_out7, decoder_2_out7);
  Register #(.width(64)) register_9 (.D(multiplexer_14_p2), .en(or_9_out), .clk(clk), .Q(r8));  // open: clr
  or or_9 (or_9_out, decoder_1_out8, decoder_2_out8);
  // Multiplexer #(.width(64)) multiplexer_14: pin names not known; wires that end beside it: demultiplexer_1_out8, multiplexer_14_p2, demultiplexer_2_out8
  Register #(.width(64)) register_10 (.D(multiplexer_15_out), .en(or_10_out), .clk(clk), .Q(r9));  // open: clr
  or or_10 (or_10_out, decoder_1_out9, decoder_2_out9);
  Multiplexer #(.width(64)) multiplexer_15 (
    .in0(demultiplexer_1_out9), .in1(demultiplexer_2_out9), .out(multiplexer_15_out));  // open: sel
  Multiplexer #(.select(4), .width(64)) multiplexer_16 (
    .in0(rax), .in1(rcx), .in2(rdx), .in3(rbx), .in4(rsp), .in5(rbp), .in6(rsi), .in7(rdi), .in8(r8),
    .in9(r9), .in10(r10), .in11(r11), .in12(r12), .in13(r13), .in14(r14), .in15({64{1'b0}}), .out(valB),
    .sel(multiplexer_3_out));
  // Multiplexer #(.width(64)) multiplexer_17: pin names not known; wires that end beside it: demultiplexer_1_out10, multiplexer_17_p2, demultiplexer_2_out10
  Register #(.width(64)) register_11 (.D(multiplexer_17_p2), .en(or_11_out), .clk(clk), .Q(r10));  // open: clr
  or or_11 (or_11_out, decoder_1_out10, decoder_2_out10);
  Register #(.width(64)) register_12 (.D(multiplexer_18_out), .en(or_12_out), .clk(clk), .Q(r11));  // open: clr
  or or_12 (or_12_out, decoder_1_out11, decoder_2_out11);
  Multiplexer #(.width(64)) multiplexer_18 (
    .in0(demultiplexer_1_out11), .in1(demultiplexer_2_out11), .out(multiplexer_18_out));  // open: sel
  Register #(.width(64)) register_13 (.D(multiplexer_19_out), .en(or_13_out), .clk(clk), .Q(r12));  // open: clr
  or or_13 (or_13_out, decoder_1_out12, decoder_2_out12);
  Multiplexer #(.width(64)) multiplexer_19 (
    .in0(demultiplexer_1_out12), .in1(demultiplexer_2_out12), .out(multiplexer_19_out));  // open: sel
  Register #(.width(64)) register_14 (.D(multiplexer_20_out), .en(or_14_out), .clk(clk), .Q(r13));  // open: clr
  or or_14 (or_14_out, decoder_1_out13, decoder_2_out13);
  Multiplexer #(.width(64)) multiplexer_20 (
    .in0(demultiplexer_1_out13), .in1(demultiplexer_2_out13), .out(multiplexer_20_out));  // open: sel
  Multiplexer #(.width(64)) multiplexer_21 (
    .in0(demultiplexer_1_out14), .in1(demultiplexer_2_out14), .out(multiplexer_21_out));  // open: sel
  Register #(.width(64)) register_15 (.D(multiplexer_21_out), .en(or_15_out), .clk(clk), .Q(r14));  // open: clr
  or or_15 (or_15_out, decoder_1_out14, decoder_2_out14);

  // Notes on the sheet:
  //   <- %rsp
endmodule
